# Fritzing sketch sketch (saved by Fritzing 0.9.5d)
breadboards: 1

parts:
  Composant1 = Arduino Nano (Rev3.0)
  DFRobot_DFPlayer_Mini1 = DFRobot DFPlayer Mini [part_number=DFR0299]
  Composant2 = PN532 Elechouse RFID NFC Module V3
  SP1 = SPEAKER [package=pcb_mount_speaker]
  TP1 = TP4056 [chip_label=TP4056 package="DIP (Dual Inline) [THT]"]  # not connected

nets:
  GND: Composant1.GND, DFRobot_DFPlayer_Mini1.GND-1, DFRobot_DFPlayer_Mini1.GND-2, Composant2.GND
  N1: Composant1.D2, Composant2.SCL
  N2: Composant1.D3, Composant2.SDA
  N3: Composant1.D11/MOSI, DFRobot_DFPlayer_Mini1.TX
  N4: Composant1.D12/MISO, DFRobot_DFPlayer_Mini1.RX
  VCC: Composant1.5V, DFRobot_DFPlayer_Mini1.VCC, Composant2.VCC
  N5: DFRobot_DFPlayer_Mini1.SPK_1, SP1.-
  N6: DFRobot_DFPlayer_Mini1.SPK_2, SP1.+

custom parts:
  PN532 Elechouse RFID NFC Module V3: NFC is a popular technology in recent years. We often heard this work while smart phone company such as Samsung or HTC introduces their latest high-end phones. Almost all the high-end phone in the market support NFC. Near field communication (NFC) is a set of standards for smart phones and similar devices to establish radio communication with each other by touching them together or bringing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
  TP4056: A DIP stand-in part for whatever IC you want. With 6 pins on a 300mil dual inline package (DIP) footprint.
